# Fritzing sketch ir_blaster_multiplexer (saved by Fritzing 0.9.3b)
circuit board: 8.46667cm x 5.64444cm
breadboards: 1

parts:
  Q1 = TRANSISTOR_NPN [package=to-92]
  Q2 = TRANSISTOR_NPN [package=to-92]
  Q3 = TRANSISTOR_NPN [package=to-92]
  Q4 = TRANSISTOR_NPN [package=to-92]
  Q5 = TRANSISTOR_NPN [package=to-92]
  Q6 = TRANSISTOR_NPN [package=to-92]
  Q7 = TRANSISTOR_NPN [package=to-92]
  Q8 = TRANSISTOR_NPN [package=to-92]
  U1 = BNC [package=bnc]
  U2 = BNC [package=bnc]
  U3 = BNC [package=bnc]
  U4 = BNC [package=bnc]
  U5 = BNC [package=bnc]
  U6 = BNC [package=bnc]
  U7 = BNC [package=bnc]
  R1 = Resistor [tolerance=±5% resistance=470 package=THT]
  R2 = Resistor [tolerance=±5% resistance=470 package=THT]
  R3 = Resistor [tolerance=±5% resistance=470 package=THT]
  R4 = Resistor [tolerance=±5% resistance=470 package=THT]
  R5 = Resistor [tolerance=±5% resistance=470 package=THT]
  R6 = Resistor [tolerance=±5% resistance=470 package=THT]
  R7 = Resistor [tolerance=±5% resistance=470 package=THT]
  R8 = Resistor [tolerance=±5% resistance=470 package=THT]
  JP1 = Header 12 [package=1x12_machine-pin-header_lock.004]

nets:
  N1: Q1.E, Q2.E, Q3.E, Q4.E, Q5.E, Q6.E, Q7.E, Q8.C
  N2: Q1.B, R1.Pin_1
  N3: Q1.C, U1.GND
  N4: Q2.B, R2.Pin_1
  N5: Q2.C, U2.GND
  N6: Q3.B, R3.Pin_1
  N7: Q3.C, U3.GND
  N8: Q4.B, R4.Pin_1
  N9: Q4.C, U4.GND
  N10: Q5.B, R5.Pin_1
  N11: Q5.C, U5.GND
  N12: Q6.B, R6.Pin_1
  N13: Q6.C, U6.GND
  N14: Q7.B, R7.Pin_1
  N15: Q7.C, U7.GND
  N16: Q8.E, JP1.12
  N17: Q8.B, R8.Pin_1
  N18: U1.OUT, U2.OUT, U3.OUT, U4.OUT, U5.OUT, U6.OUT, U7.OUT, JP1.1
  N19: R1.Pin_0, JP1.2
  N20: R2.Pin_0, JP1.3
  N21: R3.Pin_0, JP1.4
  N22: R4.Pin_0, JP1.5
  N23: R5.Pin_0, JP1.6
  N24: R6.Pin_0, JP1.7
  N25: R7.Pin_0, JP1.8
  N26: R8.Pin_0, JP1.11
